# Fritzing sketch WordClock (saved by Fritzing 0.9.4)
circuit board: 4.19567cm x 4.8985cm
breadboards: 1

parts:
  Neopixel = Header 3 [package=jst-3-pth]
  R2 = Resistor [tolerance=±5% resistance=470 package=THT]
  LDR = Header 2 [package=jst-2-pth]
  R1 = Resistor [tolerance=±5% resistance=10k package=THT]
  -Power+ = Header 2 [package=jst-2-pth]
  NodeMCU = NodeMCU V1.0
  C1 = Electrolytic Capacitor [capacitance=1000µF voltage=35V package="100 mil [THT, electrolytic]"]

nets:
  N1: Neopixel.1, LDR.1, -Power+.1, NodeMCU.Vin, C1.+
  N2: Neopixel.2, R1.Pin_1, -Power+.2, NodeMCU.GND, C1.-
  N3: Neopixel.3, R2.Pin_0
  N4: R2.Pin_1, NodeMCU.D2
  N5: LDR.2, R1.Pin_0, NodeMCU.A0

custom parts:
  NodeMCU V1.0: ESP8266 based NodeMCU
